# Fritzing sketch Schaltplan_final_Smarte_Mülltonne (saved by Fritzing 1.0.4)
breadboards: 1

parts:
  A1 = Raspberry Pi Pico2
  HC-SR04_Sensor_1 = HC-SR04 Ultrasonic Distance Sensor
  HC-SR04_Sensor_2 = HC-SR04 Ultrasonic Distance Sensor
  S2 = H-Bridge with L298N
  M3 = DC Motor [voltage_(max)=12V voltage_(min)=6V]
  M2 = DC Motor [voltage_(max)=12V voltage_(min)=6V]
  BAT1 = 12 battery [package=battery]
  A2 = 3channel line follower module
  Mod2 = KY-016 RGB Full Color LED Module [package="Breakout board"]
  S4 = Round Pushbutton
  S5 = Round Pushbutton
  Mod3 = KY-012 Active Buzzer Module [package="Breakout board"]
  S6 = Round Pushbutton
  Mod4 = KY-016 RGB Full Color LED Module [package="Breakout board"]

nets:
  N1: A1.pin_1, S4.leg1
  N2: A1.pin_2, S6.leg1
  GND: A1.pin_3, A1.pin_8, A1.pin_13, A1.pin_18, A1.pin_23, A1.pin_28, A1.pin_33, A1.pin_38, A1.pin_42, HC-SR04_Sensor_1.GND, HC-SR04_Sensor_2.GND, S2.GND, BAT1.-, A2.Pin_4, Mod2.-, S4.leg0, Mod3.-, S6.leg0, Mod4.-
  N3: A1.pin_4, S2.ENA
  N4: A1.pin_5, S2.IN1
  N5: A1.pin_6, S2.IN2
  N6: A1.pin_7, S2.IN3
  N7: A1.pin_9, S2.IN4
  N8: A1.pin_10, S2.ENB
  N9: A1.pin_11, A2.Pin_3
  N10: A1.pin_12, A2.Pin_2
  N11: A1.pin_14, A2.Pin_1
  N12: A1.pin_17, Mod3.S
  N13: A1.pin_21, Mod2.R
  N14: A1.pin_22, Mod2.G
  N15: A1.pin_24, Mod2.B
  N16: A1.pin_25, Mod4.R
  N17: A1.pin_26, Mod4.G
  N18: A1.pin_27, Mod4.B
  N19: A1.pin_29, HC-SR04_Sensor_2.TRIG
  N20: A1.pin_31, HC-SR04_Sensor_2.ECHO
  N21: A1.pin_32, HC-SR04_Sensor_1.TRIG
  N22: A1.pin_34, HC-SR04_Sensor_1.ECHO
  VCC: A1.pin_39, HC-SR04_Sensor_1.VCC, HC-SR04_Sensor_2.VCC, S2.5V, A2.Pin_5, Mod3.NC
  N23: S2.12V, S5.leg1
  N24: S2.M1-01, M3.pin_2
  N25: S2.M1-02, M3.pin_1
  N26: S2.M2-01, M2.pin_2
  N27: S2.M2-02, M2.pin_1
  N28: BAT1.+, S5.leg0

custom parts:
  Raspberry Pi Pico2: Raspberry Pi Pico 2W is our new $7 microcontroller board, built on RP2350: our new high-performance, secure microcontroller with on board WiFi.
  H-Bridge with L298N: h-bridge
  12 battery: 12V lead acid type battery, like the Husqvarna YTH2448 12V 35AH battery. This is the mini version 1/4 the size of the actual battery to be closer to typical breadboard parts (around 2in wide rathher than 7in). The pads in pcb are sized to accomidate up to 14ga wire (as these batterys will deliver high currents.)
  3channel line follower module: 3 channel line follower module.
  KY-016 RGB Full Color LED Module: KY-016 Arduino full color 5mm RGB LED, different colors can be obtained by mixing the three primary colors.
  KY-012 Active Buzzer Module: Active Piezoelectric Buzzer Module KY-012, it produces single-tone sound when signal is high. (Special thanks to vanepp for fixing the PCB holes and other errors)
